// Logisim project vrc6_cells.circ as structural Verilog: 4 circuits, main circuit vrc6_31aoi
module vrc6_31aoi (
  input  a0,
  input  a1,
  input  b0,
  input  b1,
  output x
);

  wire transistor_1_out, transistor_5_out, transistor_7_out;

  Transistor transistor_1 (.in(1'b1), .out(transistor_1_out), .gate(a0));
  Transistor transistor_2 (.in(1'b1), .out(transistor_1_out), .gate(a1));
  Transistor transistor_3 (.in(transistor_1_out), .out(x), .gate(b0));
  Transistor transistor_4 (.in(transistor_1_out), .out(x), .gate(b1));
  Transistor #(.\type ("n")) transistor_5 (.in(1'b0), .out(transistor_5_out), .gate(a0));
  Transistor #(.\type ("n")) transistor_6 (.in(transistor_5_out), .out(x), .gate(a1));
  Transistor #(.\type ("n")) transistor_7 (.in(1'b0), .out(transistor_7_out), .gate(b0));
  Transistor #(.\type ("n")) transistor_8 (.in(transistor_7_out), .out(x), .gate(b1));
endmodule

module mux2 (
  input  s0,
  input  s1,
  input  a0,
  input  a1,
  input  a2,
  input  a3,
  output x
);

  wire nand_1_out, nand_2_out, nand_3_out, nand_4_out, not_1_out, not_2_out, not_3_out, not_4_out;

  not not_1 (not_1_out, s0);
  not not_2 (not_2_out, s1);
  not not_3 (not_3_out, not_1_out);
  not not_4 (not_4_out, not_2_out);
  nand nand_1 (nand_1_out, a0, not_1_out, not_2_out);
  nand nand_2 (nand_2_out, a1, not_3_out, not_2_out);
  nand nand_3 (nand_3_out, a2, not_1_out, not_4_out);
  nand nand_4 (nand_4_out, a3, not_3_out, not_4_out);
  nand nand_5 (x, nand_1_out, nand_2_out, nand_3_out, nand_4_out);

  // Notes on the sheet:
  //   k1
  //   k2
  //   k3
  //   k4
  //   t1
  //   t2
  //   t3
  //   t4
endmodule

module vrc6_xor (
  input  a,
  input  b,
  output x
);

  wire nand_1_out, nand_2_out, or_1_out;

  nand nand_1 (nand_1_out, a, b);
  or or_1 (or_1_out, a, b);
  nand nand_2 (nand_2_out, or_1_out, nand_1_out);
  not not_1 (x, nand_2_out);
endmodule

module dec2 (
  input  n_ena,
  input  a1,
  input  a0,
  output nx0,
  output nx1,
  output nx2,
  output nx3
);

  wire not_1_out, not_2_out, not_3_out, not_4_out, not_5_out;

  not not_1 (not_1_out, n_ena);
  not not_2 (not_2_out, a1);
  not not_3 (not_3_out, a0);
  not not_4 (not_4_out, not_2_out);
  not not_5 (not_5_out, not_3_out);
  nand nand_1 (nx0, not_1_out, not_3_out, not_2_out);
  nand nand_2 (nx1, not_1_out, not_5_out, not_2_out);
  nand nand_3 (nx2, not_1_out, not_3_out, not_4_out);
  nand nand_4 (nx3, not_1_out, not_5_out, not_4_out);

  // Notes on the sheet:
  //   k1
  //   k4
  //   k5
  //   k2
  //   k3
endmodule
