// Logisim project vrc7.circ as structural Verilog: 8 circuits, main circuit ds1001
module sr_bit (
  input  value,
  input  clk1,
  input  clk2,
  output valout
);

  wire d_ff_1_qn;

  D_Flip_Flop #(.trigger("high")) d_ff_1 (.D(value), .clk(clk1), .Qn(d_ff_1_qn));  // open: Q, preset, reset
  D_Flip_Flop #(.trigger("high")) d_ff_2 (.D(d_ff_1_qn), .clk(clk2), .Qn(valout));  // open: Q, preset, reset
endmodule

module noise_lfsr (
  input  test,
  input  clk1,
  input  clk2,
  output out_4
);

  wire nor_1_out, or_1_out, sr_bit_1_valout, sr_bit_2_valout, sr_bit_3_valout, sr_bit_4_valout,
       sr_bit_5_valout, sr_bit_6_valout, sr_bit_7_valout, sr_bit_8_valout, sr_bit_9_valout, sr_bit_10_valout,
       sr_bit_11_valout, sr_bit_12_valout, sr_bit_13_valout, sr_bit_14_valout, sr_bit_15_valout,
       sr_bit_16_valout, sr_bit_17_valout, sr_bit_18_valout, sr_bit_19_valout, sr_bit_20_valout,
       sr_bit_21_valout, sr_bit_22_valout, xor_1_out;

  sr_bit sr_bit_1 (.value(or_1_out), .clk1(clk1), .clk2(clk2), .valout(sr_bit_1_valout));
  sr_bit sr_bit_2 (.value(sr_bit_1_valout), .clk1(clk1), .clk2(clk2), .valout(sr_bit_2_valout));
  sr_bit sr_bit_3 (.value(sr_bit_2_valout), .clk1(clk1), .clk2(clk2), .valout(sr_bit_3_valout));
  sr_bit sr_bit_4 (.value(sr_bit_3_valout), .clk1(clk1), .clk2(clk2), .valout(sr_bit_4_valout));
  sr_bit sr_bit_5 (.value(sr_bit_4_valout), .clk1(clk1), .clk2(clk2), .valout(sr_bit_5_valout));
  sr_bit sr_bit_6 (.value(sr_bit_5_valout), .clk1(clk1), .clk2(clk2), .valout(sr_bit_6_valout));
  sr_bit sr_bit_7 (.value(sr_bit_6_valout), .clk1(clk1), .clk2(clk2), .valout(sr_bit_7_valout));
  sr_bit sr_bit_8 (.value(sr_bit_7_valout), .clk1(clk1), .clk2(clk2), .valout(sr_bit_8_valout));
  sr_bit sr_bit_9 (.value(sr_bit_8_valout), .clk1(clk1), .clk2(clk2), .valout(sr_bit_9_valout));
  sr_bit sr_bit_10 (.value(sr_bit_9_valout), .clk1(clk1), .clk2(clk2), .valout(sr_bit_10_valout));
  sr_bit sr_bit_11 (.value(sr_bit_10_valout), .clk1(clk1), .clk2(clk2), .valout(sr_bit_11_valout));
  sr_bit sr_bit_12 (.value(sr_bit_11_valout), .clk1(clk1), .clk2(clk2), .valout(sr_bit_12_valout));
  sr_bit sr_bit_13 (.value(sr_bit_12_valout), .clk1(clk1), .clk2(clk2), .valout(sr_bit_13_valout));
  sr_bit sr_bit_14 (.value(sr_bit_13_valout), .clk1(clk1), .clk2(clk2), .valout(sr_bit_14_valout));
  sr_bit sr_bit_15 (.value(sr_bit_14_valout), .clk1(clk1), .clk2(clk2), .valout(sr_bit_15_valout));
  sr_bit sr_bit_16 (.value(sr_bit_15_valout), .clk1(clk1), .clk2(clk2), .valout(sr_bit_16_valout));
  sr_bit sr_bit_17 (.value(sr_bit_16_valout), .clk1(clk1), .clk2(clk2), .valout(sr_bit_17_valout));
  sr_bit sr_bit_18 (.value(sr_bit_17_valout), .clk1(clk1), .clk2(clk2), .valout(sr_bit_18_valout));
  sr_bit sr_bit_19 (.value(sr_bit_18_valout), .clk1(clk1), .clk2(clk2), .valout(sr_bit_19_valout));
  sr_bit sr_bit_20 (.value(sr_bit_19_valout), .clk1(clk1), .clk2(clk2), .valout(sr_bit_20_valout));
  sr_bit sr_bit_21 (.value(sr_bit_20_valout), .clk1(clk1), .clk2(clk2), .valout(sr_bit_21_valout));
  sr_bit sr_bit_22 (.value(sr_bit_21_valout), .clk1(clk1), .clk2(clk2), .valout(sr_bit_22_valout));
  sr_bit sr_bit_23 (.value(sr_bit_22_valout), .clk1(clk1), .clk2(clk2), .valout(out_4));
  nor nor_1 (nor_1_out, sr_bit_1_valout, sr_bit_2_valout, sr_bit_3_valout, sr_bit_4_valout, sr_bit_5_valout, sr_bit_6_valout, sr_bit_7_valout, sr_bit_8_valout, sr_bit_9_valout, sr_bit_10_valout, sr_bit_11_valout, sr_bit_12_valout, sr_bit_13_valout, sr_bit_14_valout, sr_bit_15_valout, sr_bit_16_valout, sr_bit_17_valout, sr_bit_18_valout, sr_bit_19_valout, sr_bit_20_valout, sr_bit_21_valout, sr_bit_22_valout, out_4);
  xor xor_1 (xor_1_out, sr_bit_9_valout, out_4);
  or or_1 (or_1_out, test, nor_1_out, xor_1_out);
endmodule

module reg_bit (
  input  value,
  input  write,
  input  n_write,
  input  reset,
  output valout
);

  wire controlled_buffer_1_out, d_ff_1_qn, nor_1_out;

  assign controlled_buffer_1_out = write ? value : 1'bz;  // Controlled_Buffer controlled_buffer_1
  D_Flip_Flop #(.trigger("high")) d_ff_1 (
    .D(controlled_buffer_1_out), .clk(1'b1), .Qn(d_ff_1_qn));  // open: Q, preset, reset
  assign controlled_buffer_1_out = n_write ? nor_1_out : 1'bz;  // Controlled_Buffer controlled_buffer_2
  not not_1 (valout, d_ff_1_qn);
  nor nor_1 (nor_1_out, d_ff_1_qn, reset);
endmodule

module ds1001 (
);


  // Notes on the sheet:
  //   Yamaha DS1001 (VRC7)
endmodule

module reg_bit2 (
  input  value,
  input  write,
  input  n_write,
  input  reset,
  input  oe,
  output valout
);

  wire controlled_buffer_1_out, controlled_buffer_3_out, d_ff_1_qn, nor_1_out;

  assign controlled_buffer_1_out = write ? value : 1'bz;  // Controlled_Buffer controlled_buffer_1
  assign controlled_buffer_1_out = n_write ? nor_1_out : 1'bz;  // Controlled_Buffer controlled_buffer_2
  D_Flip_Flop #(.trigger("high")) d_ff_1 (
    .D(controlled_buffer_1_out), .clk(1'b1), .Qn(d_ff_1_qn));  // open: Q, preset, reset
  nor nor_1 (nor_1_out, d_ff_1_qn, reset);
  assign controlled_buffer_3_out = nor_1_out ? 1'b1 : 1'bz;  // Controlled_Buffer controlled_buffer_3
  assign controlled_buffer_3_out = d_ff_1_qn ? 1'b0 : 1'bz;  // Controlled_Buffer controlled_buffer_4
  assign valout = oe ? controlled_buffer_3_out : 1'bz;  // Controlled_Buffer controlled_buffer_5
endmodule

module reg_handler (
  input  value,
  input  write,
  input  n_write,
  input  and_val,
  input  clk1,
  input  clk2,
  output valout,
  output n_valout
);

  wire and_1_out, controlled_buffer_1_out, sr_bit_1_valout;

  assign controlled_buffer_1_out = write ? value : 1'bz;  // Controlled_Buffer controlled_buffer_1
  assign controlled_buffer_1_out = n_write ? sr_bit_1_valout : 1'bz;  // Controlled_Buffer controlled_buffer_2
  sr_bit sr_bit_1 (.value(controlled_buffer_1_out), .clk1(clk1), .clk2(clk2), .valout(sr_bit_1_valout));
  and and_1 (and_1_out, sr_bit_1_valout, and_val);
  buf buffer_1 (valout, and_1_out);
  not not_1 (n_valout, and_1_out);
endmodule

module registers (
  input  clk1,
  input  clk2,
  input  sel_mod,
  input  sel_car,
  input  sel_chn,
  input  reset,
  input  write_signal1,
  input  write_signal2,
  input  [7:0] databus,
  output [3:0] multi,
  output ksr,
  output sustain,
  output vibrato,
  output tremolo,
  output [5:0] tl,
  output [1:0] ksl,
  output [2:0] feedback,
  output wf_mod,
  output wf_car,
  output [3:0] decay,
  output [3:0] attack,
  output [3:0] release_rate,
  output [3:0] sustain_level,
  output rhythm,
  output bass_drum,
  output snare_drum,
  output tom_tom,
  output top_cymbal,
  output high_hat,
  output test0,
  output test1,
  output test2,
  output test3
);

  wire not_1_out, not_2_out, reg_addr_decoder_1_addr_0, reg_addr_decoder_1_addr_1, reg_addr_decoder_1_addr_2,
       reg_addr_decoder_1_addr_3, reg_addr_decoder_1_addr_4, reg_addr_decoder_1_addr_5,
       reg_addr_decoder_1_addr_6, reg_addr_decoder_1_addr_7, reg_addr_decoder_1_addr_e,
       reg_addr_decoder_1_addr_f, reg_handler_1_n_valout, reg_handler_1_valout, reg_handler_2_n_valout,
       reg_handler_2_valout, reg_handler_3_n_valout, reg_handler_3_valout, reg_handler_4_n_valout,
       reg_handler_4_valout, reg_handler_5_n_valout, reg_handler_5_valout, reg_handler_6_n_valout,
       reg_handler_6_valout, reg_handler_7_n_valout, reg_handler_7_valout, reg_handler_8_n_valout,
       reg_handler_8_valout, reg_handler_9_n_valout, reg_handler_9_valout, reg_handler_10_n_valout,
       reg_handler_10_valout;

  not not_1 (not_1_out, write_signal2);
  not not_2 (not_2_out, not_1_out);
  reg_addr_decoder reg_addr_decoder_1 (
    .in_1(databus), .addr_f(reg_addr_decoder_1_addr_f), .addr_e(reg_addr_decoder_1_addr_e),
    .addr_0(reg_addr_decoder_1_addr_0), .addr_1(reg_addr_decoder_1_addr_1),
    .addr_2(reg_addr_decoder_1_addr_2), .addr_3(reg_addr_decoder_1_addr_3),
    .addr_4(reg_addr_decoder_1_addr_4), .addr_5(reg_addr_decoder_1_addr_5),
    .addr_6(reg_addr_decoder_1_addr_6), .addr_7(reg_addr_decoder_1_addr_7));
  reg_bit2 reg_bit2_1 (
    .value(databus[7]), .write(reg_handler_5_valout), .n_write(reg_handler_5_n_valout), .reset(reset),
    .oe(sel_car), .valout(sustain_level[3]));
  reg_bit2 reg_bit2_2 (
    .value(databus[6]), .write(reg_handler_5_valout), .n_write(reg_handler_5_n_valout), .reset(reset),
    .oe(sel_car), .valout(sustain_level[2]));
  reg_bit2 reg_bit2_3 (
    .value(databus[5]), .write(reg_handler_5_valout), .n_write(reg_handler_5_n_valout), .reset(reset),
    .oe(sel_car), .valout(sustain_level[1]));
  reg_bit2 reg_bit2_4 (
    .value(databus[4]), .write(reg_handler_5_valout), .n_write(reg_handler_5_n_valout), .reset(reset),
    .oe(sel_car), .valout(sustain_level[0]));
  reg_bit2 reg_bit2_5 (
    .value(databus[3]), .write(reg_handler_5_valout), .n_write(reg_handler_5_n_valout), .reset(reset),
    .oe(sel_car), .valout(release_rate[3]));
  reg_bit2 reg_bit2_6 (
    .value(databus[2]), .write(reg_handler_5_valout), .n_write(reg_handler_5_n_valout), .reset(reset),
    .oe(sel_car), .valout(release_rate[2]));
  reg_bit2 reg_bit2_7 (
    .value(databus[1]), .write(reg_handler_5_valout), .n_write(reg_handler_5_n_valout), .reset(reset),
    .oe(sel_car), .valout(release_rate[1]));
  reg_bit2 reg_bit2_8 (
    .value(databus[0]), .write(reg_handler_5_valout), .n_write(reg_handler_5_n_valout), .reset(reset),
    .oe(sel_car), .valout(release_rate[0]));
  reg_handler reg_handler_1 (
    .value(reg_addr_decoder_1_addr_3), .write(not_1_out), .n_write(not_2_out), .and_val(write_signal1),
    .clk1(clk1), .clk2(clk2), .valout(reg_handler_1_valout), .n_valout(reg_handler_1_n_valout));
  reg_handler reg_handler_2 (
    .value(reg_addr_decoder_1_addr_4), .write(not_1_out), .n_write(not_2_out), .and_val(write_signal1),
    .clk1(clk1), .clk2(clk2), .valout(reg_handler_2_valout), .n_valout(reg_handler_2_n_valout));
  reg_handler reg_handler_3 (
    .value(reg_addr_decoder_1_addr_5), .write(not_1_out), .n_write(not_2_out), .and_val(write_signal1),
    .clk1(clk1), .clk2(clk2), .valout(reg_handler_3_valout), .n_valout(reg_handler_3_n_valout));
  reg_handler reg_handler_4 (
    .value(reg_addr_decoder_1_addr_6), .write(not_1_out), .n_write(not_2_out), .and_val(write_signal1),
    .clk1(clk1), .clk2(clk2), .valout(reg_handler_4_valout), .n_valout(reg_handler_4_n_valout));
  reg_handler reg_handler_5 (
    .value(reg_addr_decoder_1_addr_7), .write(not_1_out), .n_write(not_2_out), .and_val(write_signal1),
    .clk1(clk1), .clk2(clk2), .valout(reg_handler_5_valout), .n_valout(reg_handler_5_n_valout));
  reg_bit2 reg_bit2_9 (
    .value(databus[7]), .write(reg_handler_4_valout), .n_write(reg_handler_4_n_valout), .reset(reset),
    .oe(sel_mod), .valout(sustain_level[3]));
  reg_bit2 reg_bit2_10 (
    .value(databus[6]), .write(reg_handler_4_valout), .n_write(reg_handler_4_n_valout), .reset(reset),
    .oe(sel_mod), .valout(sustain_level[2]));
  reg_bit2 reg_bit2_11 (
    .value(databus[5]), .write(reg_handler_4_valout), .n_write(reg_handler_4_n_valout), .reset(reset),
    .oe(sel_mod), .valout(sustain_level[1]));
  reg_bit2 reg_bit2_12 (
    .value(databus[4]), .write(reg_handler_4_valout), .n_write(reg_handler_4_n_valout), .reset(reset),
    .oe(sel_mod), .valout(sustain_level[0]));
  reg_bit2 reg_bit2_13 (
    .value(databus[3]), .write(reg_handler_4_valout), .n_write(reg_handler_4_n_valout), .reset(reset),
    .oe(sel_mod), .valout(release_rate[3]));
  reg_bit2 reg_bit2_14 (
    .value(databus[2]), .write(reg_handler_4_valout), .n_write(reg_handler_4_n_valout), .reset(reset),
    .oe(sel_mod), .valout(release_rate[2]));
  reg_bit2 reg_bit2_15 (
    .value(databus[1]), .write(reg_handler_4_valout), .n_write(reg_handler_4_n_valout), .reset(reset),
    .oe(sel_mod), .valout(release_rate[1]));
  reg_bit2 reg_bit2_16 (
    .value(databus[0]), .write(reg_handler_4_valout), .n_write(reg_handler_4_n_valout), .reset(reset),
    .oe(sel_mod), .valout(release_rate[0]));
  reg_handler reg_handler_6 (
    .value(reg_addr_decoder_1_addr_f), .write(not_1_out), .n_write(not_2_out), .and_val(write_signal1),
    .clk1(clk1), .clk2(clk2), .valout(reg_handler_6_valout), .n_valout(reg_handler_6_n_valout));
  reg_handler reg_handler_7 (
    .value(reg_addr_decoder_1_addr_e), .write(not_1_out), .n_write(not_2_out), .and_val(write_signal1),
    .clk1(clk1), .clk2(clk2), .valout(reg_handler_7_valout), .n_valout(reg_handler_7_n_valout));
  reg_handler reg_handler_8 (
    .value(reg_addr_decoder_1_addr_0), .write(not_1_out), .n_write(not_2_out), .and_val(write_signal1),
    .clk1(clk1), .clk2(clk2), .valout(reg_handler_8_valout), .n_valout(reg_handler_8_n_valout));
  reg_handler reg_handler_9 (
    .value(reg_addr_decoder_1_addr_1), .write(not_1_out), .n_write(not_2_out), .and_val(write_signal1),
    .clk1(clk1), .clk2(clk2), .valout(reg_handler_9_valout), .n_valout(reg_handler_9_n_valout));
  reg_handler reg_handler_10 (
    .value(reg_addr_decoder_1_addr_2), .write(not_1_out), .n_write(not_2_out), .and_val(write_signal1),
    .clk1(clk1), .clk2(clk2), .valout(reg_handler_10_valout), .n_valout(reg_handler_10_n_valout));
  reg_bit2 reg_bit2_17 (
    .value(databus[7]), .write(reg_handler_3_valout), .n_write(reg_handler_3_n_valout), .reset(reset),
    .oe(sel_car), .valout(attack[3]));
  reg_bit2 reg_bit2_18 (
    .value(databus[6]), .write(reg_handler_3_valout), .n_write(reg_handler_3_n_valout), .reset(reset),
    .oe(sel_car), .valout(attack[2]));
  reg_bit2 reg_bit2_19 (
    .value(databus[5]), .write(reg_handler_3_valout), .n_write(reg_handler_3_n_valout), .reset(reset),
    .oe(sel_car), .valout(attack[1]));
  reg_bit2 reg_bit2_20 (
    .value(databus[4]), .write(reg_handler_3_valout), .n_write(reg_handler_3_n_valout), .reset(reset),
    .oe(sel_car), .valout(attack[0]));
  reg_bit2 reg_bit2_21 (
    .value(databus[3]), .write(reg_handler_3_valout), .n_write(reg_handler_3_n_valout), .reset(reset),
    .oe(sel_car), .valout(decay[3]));
  reg_bit2 reg_bit2_22 (
    .value(databus[2]), .write(reg_handler_3_valout), .n_write(reg_handler_3_n_valout), .reset(reset),
    .oe(sel_car), .valout(decay[2]));
  reg_bit2 reg_bit2_23 (
    .value(databus[1]), .write(reg_handler_3_valout), .n_write(reg_handler_3_n_valout), .reset(reset),
    .oe(sel_car), .valout(decay[1]));
  reg_bit2 reg_bit2_24 (
    .value(databus[0]), .write(reg_handler_3_valout), .n_write(reg_handler_3_n_valout), .reset(reset),
    .oe(sel_car), .valout(decay[0]));
  reg_bit2 reg_bit2_25 (
    .value(databus[7]), .write(reg_handler_2_valout), .n_write(reg_handler_2_n_valout), .reset(reset),
    .oe(sel_mod), .valout(attack[3]));
  reg_bit2 reg_bit2_26 (
    .value(databus[6]), .write(reg_handler_2_valout), .n_write(reg_handler_2_n_valout), .reset(reset),
    .oe(sel_mod), .valout(attack[2]));
  reg_bit2 reg_bit2_27 (
    .value(databus[5]), .write(reg_handler_2_valout), .n_write(reg_handler_2_n_valout), .reset(reset),
    .oe(sel_mod), .valout(attack[1]));
  reg_bit2 reg_bit2_28 (
    .value(databus[4]), .write(reg_handler_2_valout), .n_write(reg_handler_2_n_valout), .reset(reset),
    .oe(sel_mod), .valout(attack[0]));
  reg_bit2 reg_bit2_29 (
    .value(databus[3]), .write(reg_handler_2_valout), .n_write(reg_handler_2_n_valout), .reset(reset),
    .oe(sel_mod), .valout(decay[3]));
  reg_bit2 reg_bit2_30 (
    .value(databus[2]), .write(reg_handler_2_valout), .n_write(reg_handler_2_n_valout), .reset(reset),
    .oe(sel_mod), .valout(decay[2]));
  reg_bit2 reg_bit2_31 (
    .value(databus[1]), .write(reg_handler_2_valout), .n_write(reg_handler_2_n_valout), .reset(reset),
    .oe(sel_mod), .valout(decay[1]));
  reg_bit2 reg_bit2_32 (
    .value(databus[0]), .write(reg_handler_2_valout), .n_write(reg_handler_2_n_valout), .reset(reset),
    .oe(sel_mod), .valout(decay[0]));
  reg_bit2 reg_bit2_33 (
    .value(databus[7]), .write(reg_handler_1_valout), .n_write(reg_handler_1_n_valout), .reset(reset),
    .oe(sel_car), .valout(ksl[1]));
  reg_bit2 reg_bit2_34 (
    .value(databus[6]), .write(reg_handler_1_valout), .n_write(reg_handler_1_n_valout), .reset(reset),
    .oe(sel_car), .valout(ksl[0]));
  reg_bit2 reg_bit2_35 (
    .value(databus[4]), .write(reg_handler_1_valout), .n_write(reg_handler_1_n_valout), .reset(reset),
    .oe(sel_chn), .valout(wf_car));
  reg_bit2 reg_bit2_36 (
    .value(databus[3]), .write(reg_handler_1_valout), .n_write(reg_handler_1_n_valout), .reset(reset),
    .oe(sel_chn), .valout(wf_mod));
  reg_bit2 reg_bit2_37 (
    .value(databus[2]), .write(reg_handler_1_valout), .n_write(reg_handler_1_n_valout), .reset(reset),
    .oe(sel_chn), .valout(feedback[2]));
  reg_bit2 reg_bit2_38 (
    .value(databus[1]), .write(reg_handler_1_valout), .n_write(reg_handler_1_n_valout), .reset(reset),
    .oe(sel_chn), .valout(feedback[1]));
  reg_bit2 reg_bit2_39 (
    .value(databus[0]), .write(reg_handler_1_valout), .n_write(reg_handler_1_n_valout), .reset(reset),
    .oe(sel_chn), .valout(feedback[0]));
  reg_bit2 reg_bit2_40 (
    .value(databus[7]), .write(reg_handler_10_valout), .n_write(reg_handler_10_n_valout), .reset(reset),
    .oe(sel_mod), .valout(ksl[1]));
  reg_bit2 reg_bit2_41 (
    .value(databus[6]), .write(reg_handler_10_valout), .n_write(reg_handler_10_n_valout), .reset(reset),
    .oe(sel_mod), .valout(ksl[0]));
  reg_bit2 reg_bit2_42 (
    .value(databus[5]), .write(reg_handler_10_valout), .n_write(reg_handler_10_n_valout), .reset(reset),
    .oe(sel_mod), .valout(tl[5]));
  reg_bit2 reg_bit2_43 (
    .value(databus[4]), .write(reg_handler_10_valout), .n_write(reg_handler_10_n_valout), .reset(reset),
    .oe(sel_mod), .valout(tl[4]));
  reg_bit2 reg_bit2_44 (
    .value(databus[3]), .write(reg_handler_10_valout), .n_write(reg_handler_10_n_valout), .reset(reset),
    .oe(sel_mod), .valout(tl[3]));
  reg_bit2 reg_bit2_45 (
    .value(databus[2]), .write(reg_handler_10_valout), .n_write(reg_handler_10_n_valout), .reset(reset),
    .oe(sel_mod), .valout(tl[2]));
  reg_bit2 reg_bit2_46 (
    .value(databus[1]), .write(reg_handler_10_valout), .n_write(reg_handler_10_n_valout), .reset(reset),
    .oe(sel_mod), .valout(tl[1]));
  reg_bit2 reg_bit2_47 (
    .value(databus[0]), .write(reg_handler_10_valout), .n_write(reg_handler_10_n_valout), .reset(reset),
    .oe(sel_mod), .valout(tl[0]));
  reg_bit2 reg_bit2_48 (
    .value(databus[7]), .write(reg_handler_9_valout), .n_write(reg_handler_9_n_valout), .reset(reset),
    .oe(sel_car), .valout(tremolo));
  reg_bit2 reg_bit2_49 (
    .value(databus[6]), .write(reg_handler_9_valout), .n_write(reg_handler_9_n_valout), .reset(reset),
    .oe(sel_car), .valout(vibrato));
  reg_bit2 reg_bit2_50 (
    .value(databus[5]), .write(reg_handler_9_valout), .n_write(reg_handler_9_n_valout), .reset(reset),
    .oe(sel_car), .valout(sustain));
  reg_bit2 reg_bit2_51 (
    .value(databus[4]), .write(reg_handler_9_valout), .n_write(reg_handler_9_n_valout), .reset(reset),
    .oe(sel_car), .valout(ksr));
  reg_bit2 reg_bit2_52 (
    .value(databus[3]), .write(reg_handler_9_valout), .n_write(reg_handler_9_n_valout), .reset(reset),
    .oe(sel_car), .valout(multi[3]));
  reg_bit2 reg_bit2_53 (
    .value(databus[2]), .write(reg_handler_9_valout), .n_write(reg_handler_9_n_valout), .reset(reset),
    .oe(sel_car), .valout(multi[2]));
  reg_bit2 reg_bit2_54 (
    .value(databus[1]), .write(reg_handler_9_valout), .n_write(reg_handler_9_n_valout), .reset(reset),
    .oe(sel_car), .valout(multi[1]));
  reg_bit2 reg_bit2_55 (
    .value(databus[0]), .write(reg_handler_9_valout), .n_write(reg_handler_9_n_valout), .reset(reset),
    .oe(sel_car), .valout(multi[0]));
  reg_bit2 reg_bit2_56 (
    .value(databus[7]), .write(reg_handler_8_valout), .n_write(reg_handler_8_n_valout), .reset(reset),
    .oe(sel_mod), .valout(tremolo));
  reg_bit2 reg_bit2_57 (
    .value(databus[6]), .write(reg_handler_8_valout), .n_write(reg_handler_8_n_valout), .reset(reset),
    .oe(sel_mod), .valout(vibrato));
  reg_bit2 reg_bit2_58 (
    .value(databus[5]), .write(reg_handler_8_valout), .n_write(reg_handler_8_n_valout), .reset(reset),
    .oe(sel_mod), .valout(sustain));
  reg_bit2 reg_bit2_59 (
    .value(databus[4]), .write(reg_handler_8_valout), .n_write(reg_handler_8_n_valout), .reset(reset),
    .oe(sel_mod), .valout(ksr));
  reg_bit2 reg_bit2_60 (
    .value(databus[3]), .write(reg_handler_8_valout), .n_write(reg_handler_8_n_valout), .reset(reset),
    .oe(sel_mod), .valout(multi[3]));
  reg_bit2 reg_bit2_61 (
    .value(databus[2]), .write(reg_handler_8_valout), .n_write(reg_handler_8_n_valout), .reset(reset),
    .oe(sel_mod), .valout(multi[2]));
  reg_bit2 reg_bit2_62 (
    .value(databus[1]), .write(reg_handler_8_valout), .n_write(reg_handler_8_n_valout), .reset(reset),
    .oe(sel_mod), .valout(multi[1]));
  reg_bit2 reg_bit2_63 (
    .value(databus[0]), .write(reg_handler_8_valout), .n_write(reg_handler_8_n_valout), .reset(reset),
    .oe(sel_mod), .valout(multi[0]));
  reg_bit reg_bit_1 (
    .value(databus[5]), .write(reg_handler_7_valout), .n_write(reg_handler_7_n_valout), .reset(reset),
    .valout(rhythm));
  reg_bit reg_bit_2 (
    .value(databus[4]), .write(reg_handler_7_valout), .n_write(reg_handler_7_n_valout), .reset(reset),
    .valout(bass_drum));
  reg_bit reg_bit_3 (
    .value(databus[3]), .write(reg_handler_7_valout), .n_write(reg_handler_7_n_valout), .reset(reset),
    .valout(snare_drum));
  reg_bit reg_bit_4 (
    .value(databus[2]), .write(reg_handler_7_valout), .n_write(reg_handler_7_n_valout), .reset(reset),
    .valout(tom_tom));
  reg_bit reg_bit_5 (
    .value(databus[1]), .write(reg_handler_7_valout), .n_write(reg_handler_7_n_valout), .reset(reset),
    .valout(top_cymbal));
  reg_bit reg_bit_6 (
    .value(databus[0]), .write(reg_handler_7_valout), .n_write(reg_handler_7_n_valout), .reset(reset),
    .valout(high_hat));
  reg_bit reg_bit_7 (
    .value(databus[3]), .write(reg_handler_6_valout), .n_write(reg_handler_6_n_valout), .reset(reset),
    .valout(test3));
  reg_bit reg_bit_8 (
    .value(databus[2]), .write(reg_handler_6_valout), .n_write(reg_handler_6_n_valout), .reset(reset),
    .valout(test2));
  reg_bit reg_bit_9 (
    .value(databus[1]), .write(reg_handler_6_valout), .n_write(reg_handler_6_n_valout), .reset(reset),
    .valout(test1));
  reg_bit reg_bit_10 (
    .value(databus[0]), .write(reg_handler_6_valout), .n_write(reg_handler_6_n_valout), .reset(reset),
    .valout(test0));
endmodule

module reg_addr_decoder (
  input  [7:0] in_1,
  output addr_f,
  output addr_e,
  output addr_0,
  output addr_1,
  output addr_2,
  output addr_3,
  output addr_4,
  output addr_5,
  output addr_6,
  output addr_7
);

  wire [7:0] not_1_out;

  assign not_1_out = ~in_1;  // NOT_Gate not_1, 8 bits wide
  nor nor_1 (addr_f, not_1_out[0], not_1_out[1], not_1_out[2], not_1_out[3], in_1[4], in_1[5], in_1[6], in_1[7]);
  nor nor_2 (addr_e, in_1[0], not_1_out[1], not_1_out[2], not_1_out[3], in_1[4], in_1[5], in_1[6], in_1[7]);
  nor nor_3 (addr_0, in_1[0], in_1[1], in_1[2], in_1[3], in_1[4], in_1[5], in_1[6], in_1[7]);
  nor nor_4 (addr_1, not_1_out[0], in_1[1], in_1[2], in_1[3], in_1[4], in_1[5], in_1[6], in_1[7]);
  nor nor_5 (addr_2, in_1[0], not_1_out[1], in_1[2], in_1[3], in_1[4], in_1[5], in_1[6], in_1[7]);
  nor nor_6 (addr_3, not_1_out[0], not_1_out[1], in_1[2], in_1[3], in_1[4], in_1[5], in_1[6], in_1[7]);
  nor nor_7 (addr_4, in_1[0], in_1[1], not_1_out[2], in_1[3], in_1[4], in_1[5], in_1[6], in_1[7]);
  nor nor_8 (addr_5, not_1_out[0], in_1[1], not_1_out[2], in_1[3], in_1[4], in_1[5], in_1[6], in_1[7]);
  nor nor_9 (addr_6, in_1[0], not_1_out[1], not_1_out[2], in_1[3], in_1[4], in_1[5], in_1[6], in_1[7]);
  nor nor_10 (addr_7, not_1_out[0], not_1_out[1], not_1_out[2], in_1[3], in_1[4], in_1[5], in_1[6], in_1[7]);
endmodule
